# Fritzing sketch OpenerPcr (saved by Fritzing 0.8.7b)
circuit board: 8cm x 6.8cm
breadboards: 7

parts:
  Peltier = Peltier Element
  External_power_supply = Power plug [part_number="Power supply"]
  External_power_supply_connector1 = female pin header, 4 pins [form="♀ (female)"]
  CT = female pin header, 2 pins [form="♀ (female)"]
  T = Temperature Sensor (Thermistor) [thermistor_type=NTC package=THT]
  R_T = Resistor [tolerance=±5% resistance=10k package=THT]
  J_RLY = female pin header, 5 pins [form="♀ (female)"]
  Arduino1 = Arduino Uno (Rev3)
  LCD = LCD screen
  R_LCD1 = Rotary Potentiometer (Small) [maximum_resistance=100kΩ package=THT]
  J_LCD = male pin header, 16 pins [form="♂ (male)"]
  J_POT = female pin header, 3 pins [form="♀ (female)"]
  R_IL1 = Resistor [tolerance=±5% resistance=1k package=THT]
  R_IL2 = Resistor [tolerance=±5% resistance=1k package=THT]
  LED_IL1_H = LED - 5mm [color="Red (633nm)" package="5 mm [THT]"]
  LED_IL1_L = LED - 5mm [color="Blue (430nm)" package="5 mm [THT]"]
  LED_IL2_L = LED - 5mm [color="Blue (430nm)" package="5 mm [THT]"]
  LED_IL2_H = LED - 5mm [color="Red (633nm)" package="5 mm [THT]"]
  J1 = female pin header, 8 pins [form="♀ (female)"]

nets:
  N1: Peltier.pin1, External_power_supply_connector1.pin3
  N2: Peltier.pin2, External_power_supply_connector1.pin4
  N3: External_power_supply.GND, External_power_supply_connector1.pin2
  N4: External_power_supply.VCC, External_power_supply_connector1.pin1
  5V: CT.pin1, T.pin_0, J_RLY.pin1, Arduino1.5V, LCD.VDD, R_LCD1.leg1, J_LCD.pin15, J_POT.pin1, LED_IL1_L.cathode, LED_IL2_L.cathode, J1.pin3, J1.pin7
  N5: CT.pin2, T.pin_1, R_T.Pin_0, Arduino1.A0
  N6: R_T.Pin_1, J_RLY.pin5, LCD.VSS, LCD.R/W, R_LCD1.leg2, J_LCD.pin12, J_LCD.pin16, J_POT.pin3, LED_IL1_H.cathode, LED_IL2_H.cathode, J1.pin2, J1.pin6
  N7: J_RLY.pin2, Arduino1.D2, R_IL1.Pin_1
  N8: J_RLY.pin3, Arduino1.D3_PWM, R_IL2.Pin_1
  N9: J_RLY.pin4, Arduino1.D5_PWM
  N10: Arduino1.D8, LCD.RS, J_LCD.pin13
  N11: Arduino1.D9_PWM, LCD.E, J_LCD.pin11
  N12: Arduino1.D10_PWM/SS, LCD.DB4, J_LCD.pin6
  N13: Arduino1.D11_PWM/MOSI, LCD.DB5, J_LCD.pin5
  N14: Arduino1.D12/MISO, LCD.DB6, J_LCD.pin4
  N15: Arduino1.D13/SCK, LCD.DB7, J_LCD.pin3
  N16: LCD.V0, R_LCD1.wiper, J_LCD.pin14, J_POT.pin2
  N17: LCD.DB0, J_LCD.pin10
  N18: LCD.DB1, J_LCD.pin9
  N19: LCD.DB2, J_LCD.pin8
  N20: LCD.DB3, J_LCD.pin7
  N21: LCD.LED+, J_LCD.pin2
  N22: LCD.LED-, J_LCD.pin1
  N23: R_IL1.Pin_0, LED_IL1_H.anode, LED_IL1_L.anode, J1.pin1, J1.pin4
  N24: R_IL2.Pin_0, LED_IL2_L.anode, LED_IL2_H.anode, J1.pin5, J1.pin8

notes:
  H bridge breakout board
  External power
  Thermistor board
  1: Termistor pin #1
  2: Termistor pin #2
  Our external power supply
  1: external power source A
  2: external power source B
  3: load pin A
  4: load pin B
  Power and ground
  1. 5 V, for powering the relay board
  2. 1: IL1, Peltier heats if HIGH
  3. 2: IL2, Peltier heats if HIGH
  4. PWM fan control
  5. GND
  Relay board
  OpenerPCR v.1.6
  DIY Bio Groningen
  Version 1.6:
  - Added LEDs that show cooling/heating
  Version 1.5:
  - Connect fan to PWM
  Version 1.4:
  - added one pin for fan on/off
  - removed H-bridge breakout board connector from PCB
  Version 1.3:
  - fixed error (again) in thermistor connection
  - removed thermistor from PCB: use the connectors for it
  Version 1.2:
  - fixed error in thermistor connection
  Version 1.1:
  - use an extra pin, to be able to turn the Peltier off
  - removed some unused connectors
  2014-04-06
